# Fritzing sketch led strip (saved by Fritzing 0.9.3b)

parts:
  Part1 = Arduino Uno (Rev3)
  Part2 = LED strip [part_number=JST-B3P-VH package=THT]

nets:
  N1: Part1.D5_PWM, Part2.DATA
  N2: Part1.5V, Part2.DC5V
  GND: Part1.GND, Part2.GND
