# Fritzing sketch programmer (saved by Fritzing 0.9.3b)
breadboards: 1
perfboards: 1

parts:
  S1 = Pushbutton [package="[THT]"]
  Part1 = FTDI Basic Programmer
  S2 = Pushbutton [package="[THT]"]
  R1 = Resistor [tolerance=±5% resistance=10k package=THT]
  U1 = ESP8266 WiFi Module [part_number=ESP8266]
  R2 = Resistor [tolerance=±5% resistance=10k package=THT]
  U2 = ESP8266 WiFi Module [part_number=ESP8266]  # not connected
  Part2 = FTDI Basic Programmer
  S3 = Pushbutton [package="[THT]"]
  S4 = Pushbutton [package="[THT]"]
  R3 = Resistor [tolerance=±5% resistance=10k package=THT]
  R4 = Resistor [tolerance=±5% resistance=10k package=THT]

nets:
  GND: S1.Pin_1, S1.Pin_2, Part1.GND, S2.Pin_1, S2.Pin_2, U1.GND, Part2.GND, S3.Pin_1, S3.Pin_2, S4.Pin_1, S4.Pin_2
  N1: S1.Pin_3, S1.Pin_4, U1.GPIO_0
  N2: Part1.RXI, U1.TXD
  N3: Part1.TXO, U1.RXD
  N4: Part1.POWER, R1.Pin_0, U1.VCC, R2.Pin_0, Part2.POWER, R3.Pin_0, R4.Pin_0
  N5: S2.Pin_3, S2.Pin_4, R1.Pin_1, U1.RST
  N6: U1.CH_PD, R2.Pin_1
  N7: S3.Pin_3, S3.Pin_4
  N8: S4.Pin_3, S4.Pin_4, R3.Pin_1

custom parts:
  ESP8266 WiFi Module: Generic WiFi Module based on the ESP8266 with onboard PCB antenna and UART communications
